# Fritzing sketch DutyCycling2 (saved by Fritzing 0.9.8b)
breadboards: 1

parts:
  MC = Arduino Uno (Rev3) - ICSP
  LED1 = LED - 5mm [color="Red (660nm)" current=30mA package="5 mm [THT]"]
  R1 = Resistor [tolerance=±5% resistance=220 package="1206 [SMD]"]
  DHT11 = Humidity and Temperature Sensor RHT03

nets:
  N1: MC.ICSP_MISO, MC.D12/MISO, LED1.anode
  5V: MC.5V, DHT11.Vcc
  N2: MC.GND, R1.Pin_0, DHT11.GND_2
  N3: MC.D8, DHT11.Data-signal
  N4: LED1.cathode, R1.Pin_1

notes:
  Connected Objects and the IoT, Watchdog based duty-cycling 2, Ilja Tihhanovski
